# Fritzing sketch LCD-schematic (saved by Fritzing 0.9.2b)
breadboards: 1

parts:
  R1 = Trimmer Potentiometer [maximum_resistance=10kΩ package=THT]
  U1 = LCD-16X2 [package=lcd-16x2]
  Part1 = Arduino Uno (Rev3)
  R2 = Resistor [tolerance=±5% resistance=100 package=THT]
  R3 = Resistor [tolerance=±5% resistance=100 package=THT]

nets:
  VSS: R1.leg1, U1.VSS, U1.R_W, U1.K, Part1.GND
  N1: R1.wiper, U1.VO
  VDD: R1.leg2, U1.VDD, Part1.5V, R3.Pin_0
  N2: U1.RS, Part1.D12/MISO
  N3: U1.E, Part1.D11_PWM/MOSI
  N4: U1.DB2, U1.DB4, Part1.D5_PWM
  N5: U1.DB5, Part1.D4
  N6: U1.DB6, Part1.D3_PWM
  N7: U1.DB7, Part1.D2
  N8: U1.A, R2.Pin_0
  N9: R2.Pin_1, R3.Pin_1
