# Fritzing sketch buttonDebounce-schematic (saved by Fritzing 0.9.2b)
breadboards: 1

parts:
  Part1 = Arduino Uno (Rev3)
  S1 = Pushbutton [package="[THT]"]
  LED1 = LED - 5mm [color="Red (633nm)" package="5 mm [THT]"]  # not connected
  R1 = Resistor [tolerance=±5% resistance=100 package=THT]
  R2 = Resistor [tolerance=±5% resistance=10k package=THT]

nets:
  N1: Part1.GND, R1.Pin_0, R2.Pin_0
  N2: Part1.D4, S1.Pin_3, S1.Pin_4, R2.Pin_1
  N3: Part1.5V, S1.Pin_1, S1.Pin_2
