# Fritzing sketch recorder (saved by Fritzing 0.9.3b)

parts:
  Voice_Recorder_ISD1820 = Microphone
  S1 = Pushbutton [package="[THT]"]
  Componente1 = Arduino Uno (Rev3)

nets:
  N1: Voice_Recorder_ISD1820.pin1, S1.Pin_4, Componente1.GND
  N2: Voice_Recorder_ISD1820.pin2, Componente1.5V
  N3: S1.Pin_2, Componente1.D11_PWM/MOSI

notes:
  GND
  VCC
  REC
  P-E
